# Fritzing sketch WetterstationSender (saved by Fritzing 0.9.0b)
breadboards: 1

parts:
  Bauteil1 = Arduino Uno (Rev3)
  RHT1 = Humidity and Temperature Sensor RHT03
  Bauteil2 = Barometric Pressure Sensor - BMP085 Breakout
  U1 = DS18B20
  R2 = Resistor [tolerance=±5% resistance=4.7k package=THT]
  R3 = Resistor [tolerance=±5% resistance=4.7k package=THT]

nets:
  N1: Bauteil1.A4/SDA, Bauteil2.SDA
  N2: Bauteil1.A5/SCL, Bauteil2.SCL
  N3: Bauteil1.D3_PWM, RHT1.Data-signal, R2.Pin_0
  N4: Bauteil1.D4, U1.DQ, R3.Pin_0
  VCC: Bauteil1.3V3, RHT1.Vcc, Bauteil2.VCC, U1.VCC, R2.Pin_1, R3.Pin_1
  GND: Bauteil1.GND, RHT1.GND_2, Bauteil2.GND, U1.GND

custom parts:
  DS18B20: Programmable Resolution 1-Wire Thermometer
